# Fritzing sketch arduino_isp (saved by Fritzing 0.9.3b)
breadboards: 1

parts:
  U1 = atmega328 [package=dip]
  C1 = Ceramic Capacitor [capacitance=100nF package="100 mil [THT, multilayer]"]
  C2 = Ceramic Capacitor [capacitance=100nF package="100 mil [THT, multilayer]"]
  XTAL1 = Crystal [frequency="16 Mhz" package=THT]
  R1 = Resistor [tolerance=±5% resistance=10k package=THT]
  Part1 = Arduino Uno (Rev3)

nets:
  N1: U1.RESET, R1.Pin_0, Part1.D10_PWM/SS
  N2: U1.VCC, R1.Pin_1
  N3: U1.GND#7, C1.0, C2.1
  N4: U1.XLAT1, C2.0, XTAL1.pin_1
  N5: U1.XLAT2, C1.1, XTAL1.pin_0
  N6: U1.D11_(PWM), Part1.D11_PWM/MOSI
  N7: U1.D12, Part1.D12/MISO
  N8: U1.D13, Part1.D13/SCK
  N9: U1.AVCC, Part1.5V
  N10: U1.GND#21, Part1.GND
