# Fritzing sketch serial (saved by Fritzing 0.9.3b)
breadboards: 1

parts:
  U1 = atmega328 [package=dip]
  C1 = Ceramic Capacitor [capacitance=100nF package="100 mil [THT, multilayer]"]
  C2 = Ceramic Capacitor [capacitance=100nF package="100 mil [THT, multilayer]"]
  XTAL1 = Crystal [frequency="16 Mhz" package=THT]
  R1 = Resistor [tolerance=±5% resistance=10k package=THT]

nets:
  N1: U1.RESET, R1.Pin_0
  N2: U1.VCC, R1.Pin_1
  N3: U1.GND#7, C1.0, C2.1
  N4: U1.XLAT1, C2.0, XTAL1.pin_1
  N5: U1.XLAT2, C1.1, XTAL1.pin_0
